// Logisim project MIPS-lite-noprobe.circ as structural Verilog: 13 circuits, main circuit main
module main (
  input  in_1,
  output c1,
  output out_3,
  output c2,
  output [5:0] Func_5_0,
  output [5:0] op_31_26
);

  wire ALUsrc, Beq_jump, C, cALU3, Clk, iszero_1_ouput, MEMtoreg, Memwrite, Regdst, Regwrite;
  wire [1:0] cALU1, cALU2, Extop;
  wire [4:0] multiplexer_1_out, rs, rt;
  wire [15:6] Imm16;
  wire [31:0] ALUout, dm_1_outdata, extender_1_b_31_0, gpr_1_rd1, gpr_1_rd2, multiplexer_2_out,
       multiplexer_3_out;

  IsZero iszero_1 (.Input(ALUout), .Ouput(iszero_1_ouput));
  Clock clock_1 (.out(Clk));
  IFU ifu_1 (
    .IfBeq(Beq_jump), .Zero(iszero_1_ouput), .Clk(Clk), .Reset(in_1),
    .Instruction({op_31_26, rs, rt, Imm16, Func_5_0}), .C1(c1), .C2(c2));  // open: PC_1, Beq_jump
  Control control_1 (
    .func_5_0(Func_5_0), .opcode_31_26(op_31_26), .Regdst(Regdst), .Alusrc(ALUsrc), .Memtoreg(MEMtoreg),
    .Regwrite(Regwrite), .Memwrite(Memwrite), .npc_sel(Beq_jump), .extop(Extop), .C(C), .cALU1(cALU1),
    .cALU2(cALU2), .cALU3(cALU3));  // open: out_3, out_4, out_16, out_17, out_18, out_19, out_20
  Multiplexer #(.width(5)) multiplexer_1 (
    .in0(rt), .in1(Imm16[15:11]), .out(multiplexer_1_out), .sel(Regdst), .en(1'b1));
  Multiplexer #(.width(32)) multiplexer_2 (
    .in0(ALUout), .in1(dm_1_outdata), .out(multiplexer_2_out), .sel(MEMtoreg), .en(1'b1));
  GPR gpr_1 (
    .Reset(in_1), .Clk(Clk), .A2(rs), .Regwrite(Regwrite), .A1(multiplexer_1_out), .A3(rt), .Rd1(gpr_1_rd1),
    .Rd2(gpr_1_rd2), .Wd(multiplexer_2_out));
  Multiplexer #(.width(32)) multiplexer_3 (
    .in0(gpr_1_rd2), .in1(extender_1_b_31_0), .out(multiplexer_3_out), .sel(ALUsrc), .en(1'b1));
  Extender extender_1 (.A_15_0({Imm16, Func_5_0}), .Extop(Extop), .B_31_0(extender_1_b_31_0));
  ALU alu_1 (
    .C(C), .A(gpr_1_rd1), .B(multiplexer_3_out), .cALU1(cALU1), .cALU2(cALU2), .cALU3(cALU3), .C_2(out_3),
    .Result(ALUout));
  DM dm_1 (
    .A_4_0(ALUout[6:2]), .inData(gpr_1_rd2), .outData(dm_1_outdata), .Memwrite(Memwrite), .Clk(Clk),
    .Reset(in_1));

  // Other names for the same wires on the sheet: Op[5:0] = op_31_26; Func[5:0] = Func_5_0; Imm16[5:0] = Func_5_0;
  //   Offset[4:0] = Imm16[10:6]; rd[4:0] = Imm16[15:11]; Reset = in_1
endmodule

module _1BitAdder (
  input  C,
  input  A,
  input  B,
  output S,
  output C_2
);

  wire and_1_out, and_2_out, xor_1_out;

  xor xor_1 (xor_1_out, C, A);
  and and_1 (and_1_out, C, A);
  xor xor_2 (S, xor_1_out, B);
  and and_2 (and_2_out, xor_1_out, B);
  or or_1 (C_2, and_1_out, and_2_out);
endmodule

module Control (
  input  [5:0] func_5_0,
  input  [5:0] opcode_31_26,
  output out_3,
  output out_4,
  output C,
  output Memtoreg,
  output npc_sel,
  output Regdst,
  output Alusrc,
  output Regwrite,
  output Memwrite,
  output [1:0] extop,
  output [1:0] cALU1,
  output [1:0] cALU2,
  output cALU3,
  output out_16,
  output out_17,
  output out_18,
  output out_19,
  output out_20
);

  and and_1 (out_3, ~opcode_31_26[5], ~opcode_31_26[4], ~opcode_31_26[3], ~opcode_31_26[2], ~opcode_31_26[1], ~opcode_31_26[0], func_5_0[5], ~func_5_0[4], ~func_5_0[3], ~func_5_0[2], ~func_5_0[1], ~func_5_0[0]);  // AND_Gate
  and and_2 (out_4, ~opcode_31_26[5], ~opcode_31_26[4], ~opcode_31_26[3], ~opcode_31_26[2], ~opcode_31_26[1], ~opcode_31_26[0], func_5_0[5], ~func_5_0[4], ~func_5_0[3], ~func_5_0[2], func_5_0[1], ~func_5_0[0]);  // AND_Gate
  and and_3 (extop[0], ~opcode_31_26[5], ~opcode_31_26[4], opcode_31_26[3], opcode_31_26[2], ~opcode_31_26[1], opcode_31_26[0]);  // AND_Gate
  and and_4 (Memtoreg, opcode_31_26[5], ~opcode_31_26[4], ~opcode_31_26[3], ~opcode_31_26[2], opcode_31_26[1], opcode_31_26[0]);  // AND_Gate
  and and_5 (Memwrite, opcode_31_26[5], ~opcode_31_26[4], opcode_31_26[3], ~opcode_31_26[2], opcode_31_26[1], opcode_31_26[0]);  // AND_Gate
  and and_6 (npc_sel, ~opcode_31_26[5], ~opcode_31_26[4], ~opcode_31_26[3], opcode_31_26[2], ~opcode_31_26[1], ~opcode_31_26[0]);  // AND_Gate
  and and_7 (cALU1[1], ~opcode_31_26[5], ~opcode_31_26[4], opcode_31_26[3], opcode_31_26[2], opcode_31_26[1], opcode_31_26[0]);  // AND_Gate
  or or_1 (Regdst, out_3, out_4);
  or or_2 (Alusrc, extop[0], Memtoreg, Memwrite, 1'b0, cALU1[1]);
  or or_3 (Regwrite, out_3, out_4, extop[0], Memtoreg, cALU1[1]);
  or or_4 (C, out_4, npc_sel);
  or or_5 (cALU1[0], out_4, npc_sel);
  not not_1 (cALU2[1], extop[0]);
  or or_6 (cALU3, extop[0], cALU1[1]);

  assign cALU2[0] = cALU2[1];
  assign extop[1] = cALU1[1];
  assign out_16 = extop[0];
  assign out_17 = Memtoreg;
  assign out_18 = Memwrite;
  assign out_19 = npc_sel;
  assign out_20 = cALU1[1];

  // Other names for the same wires on the sheet: addu = out_3; beq = npc_sel; lui = cALU1[1]; ori = extop[0];
  //   lw = Memtoreg; subu = out_4; sw = Memwrite
endmodule

module IFU (
  input  IfBeq,
  input  Zero,
  input  Clk,
  input  Reset,
  output [31:0] Instruction,
  output [29:0] PC_1,
  output C1,
  output [29:0] Beq_jump,
  output C2
);

  wire IsJump;
  wire [29:0] multiplexer_1_out, PC;
  wire [31:0] bit_extender_1_out;
  wire [31:30] n32bitsadder_1_s, n32bitsadder_2_s;

  and and_1 (IsJump, IfBeq, Zero);
  assign bit_extender_1_out = {{16{Instruction[15]}}, Instruction[15:0]};  // Bit_Extender bit_extender_1
  _32BitsAdder u_32bitsadder_1 (.C(1'b0), .A({2'b00, PC}), .B(32'h1), .S({n32bitsadder_1_s, PC_1}), .C_2(C1));
  _32BitsAdder u_32bitsadder_2 (
    .C(1'b0), .A(bit_extender_1_out), .B({2'b00, PC_1}), .S({n32bitsadder_2_s, Beq_jump}), .C_2(C2));
  Multiplexer #(.width(30)) multiplexer_1 (
    .in0(PC_1), .in1(Beq_jump), .out(multiplexer_1_out), .sel(IsJump), .en(1'b1));
  Register #(.width(30)) u_PC (.D(multiplexer_1_out), .en(1'b1), .Q(PC), .clk(Clk), .clr(Reset));
  ROM #(.addrWidth(5), .dataWidth(32)) rom_1 (.addr(PC[4:0]), .data(Instruction));  // open: sel

  // Other names for the same wires on the sheet: Inst[31:0] = Instruction

  // Notes on the sheet:
  //   contents of rom_1 (hex, n*v repeats v):
  //   34010000 34020000 3403aabb 34040010 3c05aabb 34060001 34070004 ac450000 260820 471020 a62820
  //   10240001 1000fffa 8c1f0001 3e6f022 e6e822
endmodule

// EXT
module Extender (
  input  [15:0] A_15_0,
  input  [1:0] Extop,
  output [31:0] B_31_0
);

  wire [31:0] bit_extender_1_out;

  assign bit_extender_1_out = {{16{A_15_0[15]}}, A_15_0};  // Bit_Extender bit_extender_1
  Multiplexer #(.select(2), .width(32)) multiplexer_1 (
    .in0(bit_extender_1_out), .in1({{16{1'b0}}, A_15_0}), .in2({A_15_0, {16{1'b0}}}), .in3({32{1'b0}}),
    .out(B_31_0), .sel(Extop), .en(1'b1));
endmodule

module _32BitsAdder (
  input  C,
  input  [31:0] A,
  input  [31:0] B,
  output [31:0] S,
  output C_2
);

  wire n16bitsadder_1_c_2;

  _16BitsAdder u_16bitsadder_1 (.C(C), .A16(A[15:0]), .B16(B[15:0]), .S16(S[15:0]), .C_2(n16bitsadder_1_c_2));
  _16BitsAdder u_16bitsadder_2 (.C(n16bitsadder_1_c_2), .A16(A[31:16]), .B16(B[31:16]), .S16(S[31:16]), .C_2(C_2));
endmodule

module _4BitsAdder (
  input  C,
  input  [3:0] A4,
  input  [3:0] B4,
  output [3:0] S4,
  output C_2
);

  wire n1bitadder_1_c_2, n1bitadder_2_c_2, n1bitadder_3_c_2;

  _1BitAdder u_1bitadder_1 (.C(C), .A(A4[0]), .B(B4[0]), .S(S4[0]), .C_2(n1bitadder_1_c_2));
  _1BitAdder u_1bitadder_2 (.C(n1bitadder_1_c_2), .A(A4[1]), .B(B4[1]), .S(S4[1]), .C_2(n1bitadder_2_c_2));
  _1BitAdder u_1bitadder_3 (.C(n1bitadder_2_c_2), .A(A4[2]), .B(B4[2]), .S(S4[2]), .C_2(n1bitadder_3_c_2));
  _1BitAdder u_1bitadder_4 (.C(n1bitadder_3_c_2), .A(A4[3]), .B(B4[3]), .S(S4[3]), .C_2(C_2));
endmodule

module _16BitsAdder (
  input  C,
  input  [15:0] A16,
  input  [15:0] B16,
  output [15:0] S16,
  output C_2
);

  wire n4bitsadder_1_c_2, n4bitsadder_2_c_2, n4bitsadder_3_c_2;

  _4BitsAdder u_4bitsadder_1 (.C(C), .A4(A16[3:0]), .B4(B16[3:0]), .S4(S16[3:0]), .C_2(n4bitsadder_1_c_2));
  _4BitsAdder u_4bitsadder_2 (
    .C(n4bitsadder_1_c_2), .A4(A16[7:4]), .B4(B16[7:4]), .S4(S16[7:4]), .C_2(n4bitsadder_2_c_2));
  _4BitsAdder u_4bitsadder_3 (
    .C(n4bitsadder_2_c_2), .A4(A16[11:8]), .B4(B16[11:8]), .S4(S16[11:8]), .C_2(n4bitsadder_3_c_2));
  _4BitsAdder u_4bitsadder_4 (.C(n4bitsadder_3_c_2), .A4(A16[15:12]), .B4(B16[15:12]), .S4(S16[15:12]), .C_2(C_2));
endmodule

module ALU (
  input  C,
  input  [31:0] A,
  input  [1:0] cALU1,
  input  [31:0] B,
  input  cALU3,
  input  [1:0] cALU2,
  output C_2,
  output [31:0] Result
);

  wire [31:0] and_1_out, multiplexer_1_out, multiplexer_2_out, n32bitsadder_1_s, not_1_out, not_2_out,
       or_1_out;

  assign not_1_out = ~B;  // NOT_Gate not_1, 32 bits wide
  assign or_1_out = A | B;  // OR_Gate or_1, 32 bits wide
  assign and_1_out = A & B;  // AND_Gate and_1, 32 bits wide
  assign not_2_out = ~B;  // NOT_Gate not_2, 32 bits wide
  Multiplexer #(.select(2), .width(32)) multiplexer_1 (
    .in0(B), .in1(not_1_out), .in2({32{1'b0}}), .in3({32{1'b1}}), .out(multiplexer_1_out), .sel(cALU1),
    .en(1'b1));
  Multiplexer #(.select(2), .width(32)) multiplexer_2 (
    .in0(or_1_out), .in1(and_1_out), .in2(not_2_out), .in3(B), .out(multiplexer_2_out), .sel(cALU2), .en(1'b1));
  _32BitsAdder u_32bitsadder_1 (.C(C), .A(A), .B(multiplexer_1_out), .S(n32bitsadder_1_s), .C_2(C_2));
  Multiplexer #(.width(32)) multiplexer_3 (
    .in0(n32bitsadder_1_s), .in1(multiplexer_2_out), .out(Result), .sel(cALU3), .en(1'b1));
endmodule

module GPR (
  input  Reset,
  input  Clk,
  input  [31:0] Wd,
  input  [4:0] A2,
  input  Regwrite,
  input  [4:0] A1,
  input  [4:0] A3,
  output [31:0] Rd1,
  output [31:0] Rd2
);

  wire [7:0] demultiplexer_1_out0, demultiplexer_1_out8, demultiplexer_1_out16, demultiplexer_1_out24;
  wire [31:0] R0, R1, R2, R3, R4, R5, R6, R7, R8, R9, R10, R11, R12, R13, R14, R15, R16, R17, R18, R19, R20,
       R21, R22, R23, R24, R25, R26, R27, R28, R29, R30, R31;

  Demultiplexer #(.select(5)) demultiplexer_1 (
    .out0(demultiplexer_1_out0[0]), .out1(demultiplexer_1_out0[1]), .out2(demultiplexer_1_out0[2]),
    .out3(demultiplexer_1_out0[3]), .out4(demultiplexer_1_out0[4]), .out5(demultiplexer_1_out0[5]),
    .out6(demultiplexer_1_out0[6]), .out7(demultiplexer_1_out0[7]), .out8(demultiplexer_1_out8[0]),
    .out9(demultiplexer_1_out8[1]), .out10(demultiplexer_1_out8[2]), .out11(demultiplexer_1_out8[3]),
    .out12(demultiplexer_1_out8[4]), .out13(demultiplexer_1_out8[5]), .out14(demultiplexer_1_out8[6]),
    .out15(demultiplexer_1_out8[7]), .out16(demultiplexer_1_out16[0]), .out17(demultiplexer_1_out16[1]),
    .out18(demultiplexer_1_out16[2]), .out19(demultiplexer_1_out16[3]), .out20(demultiplexer_1_out16[4]),
    .out21(demultiplexer_1_out16[5]), .out22(demultiplexer_1_out16[6]), .out23(demultiplexer_1_out16[7]),
    .out24(demultiplexer_1_out24[0]), .out25(demultiplexer_1_out24[1]), .out26(demultiplexer_1_out24[2]),
    .out27(demultiplexer_1_out24[3]), .out28(demultiplexer_1_out24[4]), .out29(demultiplexer_1_out24[5]),
    .out30(demultiplexer_1_out24[6]), .out31(demultiplexer_1_out24[7]), .in(Regwrite), .sel(A1), .en(1'b1));
  GPR_8 gpr_8_1 (
    .Reset_8(Reset), .Clk_8(Clk), .Regwrite_8(demultiplexer_1_out0), .Input_8_2(Wd), .Input_8_3(Wd),
    .Input_8_4(Wd), .Input_8_5(Wd), .Input_8_6(Wd), .Input_8_7(Wd), .Input_8_8(Wd), .Output_8(R0),
    .Output_8_2(R1), .Output_8_3(R2), .Output_8_4(R3), .Output_8_5(R4), .Output_8_6(R5), .Output_8_7(R6),
    .Output_8_8(R7));  // open: Input_8
  GPR_8 gpr_8_2 (
    .Reset_8(Reset), .Clk_8(Clk), .Regwrite_8(demultiplexer_1_out8), .Input_8(Wd), .Input_8_2(Wd),
    .Input_8_3(Wd), .Input_8_4(Wd), .Input_8_5(Wd), .Input_8_6(Wd), .Input_8_7(Wd), .Input_8_8(Wd),
    .Output_8(R8), .Output_8_2(R9), .Output_8_3(R10), .Output_8_4(R11), .Output_8_5(R12), .Output_8_6(R13),
    .Output_8_7(R14), .Output_8_8(R15));
  GPR_8 gpr_8_3 (
    .Reset_8(Reset), .Clk_8(Clk), .Regwrite_8(demultiplexer_1_out16), .Input_8(Wd), .Input_8_2(Wd),
    .Input_8_3(Wd), .Input_8_4(Wd), .Input_8_5(Wd), .Input_8_6(Wd), .Input_8_7(Wd), .Input_8_8(Wd),
    .Output_8(R16), .Output_8_2(R17), .Output_8_3(R18), .Output_8_4(R19), .Output_8_5(R20), .Output_8_6(R21),
    .Output_8_7(R22), .Output_8_8(R23));
  GPR_8 gpr_8_4 (
    .Reset_8(Reset), .Clk_8(Clk), .Regwrite_8(demultiplexer_1_out24), .Input_8(Wd), .Input_8_2(Wd),
    .Input_8_3(Wd), .Input_8_4(Wd), .Input_8_5(Wd), .Input_8_6(Wd), .Input_8_7(Wd), .Input_8_8(Wd),
    .Output_8(R24), .Output_8_2(R25), .Output_8_3(R26), .Output_8_4(R27), .Output_8_5(R28), .Output_8_6(R29),
    .Output_8_7(R30), .Output_8_8(R31));
  Multiplexer #(.select(5), .width(32)) multiplexer_1 (
    .in0(R0), .in1(R1), .in2(R2), .in3(R3), .in4(R4), .in5(R5), .in6(R6), .in7(R7), .in8(R8), .in9(R9),
    .in10(R10), .in11(R11), .in12(R12), .in13(R13), .in14(R14), .in15(R15), .in16(R16), .in17(R17),
    .in18(R18), .in19(R19), .in20(R20), .in21(R21), .in22(R22), .in23(R23), .in24(R24), .in25(R25),
    .in26(R26), .in27(R27), .in28(R28), .in29(R29), .in30(R30), .in31(R31), .out(Rd1), .sel(A2), .en(1'b1));
  Multiplexer #(.select(5), .width(32)) multiplexer_2 (
    .in0(R0), .in1(R1), .in2(R2), .in3(R3), .in4(R4), .in5(R5), .in6(R6), .in7(R7), .in8(R8), .in9(R9),
    .in10(R10), .in11(R11), .in12(R12), .in13(R13), .in14(R14), .in15(R15), .in16(R16), .in17(R17),
    .in18(R18), .in19(R19), .in20(R20), .in21(R21), .in22(R22), .in23(R23), .in24(R24), .in25(R25),
    .in26(R26), .in27(R27), .in28(R28), .in29(R29), .in30(R30), .in31(R31), .out(Rd2), .sel(A3), .en(1'b1));

  // Other names for the same wires on the sheet: Input[31:0] = Wd
endmodule

module GPR_8 (
  input  Reset_8,
  input  Clk_8,
  input  [7:0] Regwrite_8,
  input  [31:0] Input_8,
  input  [31:0] Input_8_2,
  input  [31:0] Input_8_3,
  input  [31:0] Input_8_4,
  input  [31:0] Input_8_5,
  input  [31:0] Input_8_6,
  input  [31:0] Input_8_7,
  input  [31:0] Input_8_8,
  output [31:0] Output_8,
  output [31:0] Output_8_2,
  output [31:0] Output_8_3,
  output [31:0] Output_8_4,
  output [31:0] Output_8_5,
  output [31:0] Output_8_6,
  output [31:0] Output_8_7,
  output [31:0] Output_8_8
);

  Register #(.width(32), .trigger("falling")) register_1 (
    .D(Input_8), .en(Regwrite_8[0]), .Q(Output_8), .clk(Clk_8), .clr(Reset_8));
  Register #(.width(32), .trigger("falling")) register_2 (
    .D(Input_8_2), .en(Regwrite_8[1]), .Q(Output_8_2), .clk(Clk_8), .clr(Reset_8));
  Register #(.width(32), .trigger("falling")) register_3 (
    .D(Input_8_3), .en(Regwrite_8[2]), .Q(Output_8_3), .clk(Clk_8), .clr(Reset_8));
  Register #(.width(32), .trigger("falling")) register_4 (
    .D(Input_8_4), .en(Regwrite_8[3]), .Q(Output_8_4), .clk(Clk_8), .clr(Reset_8));
  Register #(.width(32), .trigger("falling")) register_5 (
    .D(Input_8_5), .en(Regwrite_8[4]), .Q(Output_8_5), .clk(Clk_8), .clr(Reset_8));
  Register #(.width(32), .trigger("falling")) register_6 (
    .D(Input_8_6), .en(Regwrite_8[5]), .Q(Output_8_6), .clk(Clk_8), .clr(Reset_8));
  Register #(.width(32), .trigger("falling")) register_7 (
    .D(Input_8_7), .en(Regwrite_8[6]), .Q(Output_8_7), .clk(Clk_8), .clr(Reset_8));
  Register #(.width(32), .trigger("falling")) register_8 (
    .D(Input_8_8), .en(Regwrite_8[7]), .Q(Output_8_8), .clk(Clk_8), .clr(Reset_8));
endmodule

module IsZero (
  input  [31:0] Input,
  output Ouput
);

  wire or_1_out;

  or or_1 (or_1_out, Input[0], Input[1], Input[2], Input[3], Input[4], Input[5], Input[6], Input[7], Input[8], Input[9], Input[10], Input[11], Input[12], Input[13], Input[14], Input[15], Input[17], Input[18], Input[19], Input[20], Input[21], Input[22], Input[23], Input[24], Input[25], Input[26], Input[27], Input[28], Input[29], Input[30], Input[31], Input[16]);
  not not_1 (Ouput, or_1_out);
endmodule

module DM (
  input  [4:0] A_4_0,
  input  [31:0] inData,
  input  Reset,
  input  Memwrite,
  input  Clk,
  output [31:0] outData
);

  wire not_1_out;

  not not_1 (not_1_out, Clk);
  RAM #(.addrWidth(5), .dataWidth(32), .bus("separate")) ram_1 (
    .addr(A_4_0), .din(inData), .data(outData), .str(Memwrite), .sel(1'b1), .clk(not_1_out), .ld(1'b1),
    .clr(Reset));
endmodule
